// Logisim project Calculator Fidan Ismayilova.circ as structural Verilog: 10 circuits, main circuit main
module main (
  input  [3:0] in_1,
  input  [3:0] in_2,
  input  [3:0] in_3,
  input  [3:0] in_4
);

  wire _0_out, _1_out, _2_out, _3_out, _4_out, _5_out, _6_out, _7_out, _8_out, _9_out, A___B_out, and_1_out,
       and_2_out, and_3_out, and_4_out, and_5_out, and_6_out, and_7_out, and_8_out, and_9_out, and_10_out,
       and_11_out, and_12_out, and_13_out, and_14_out, and_15_out, and_16_out, and_17_out, and_18_out,
       and_19_out, and_20_out, and_21_out, and_22_out, and_23_out, and_24_out, B___A_out,
       bcd_adder_2_carry_out, bcd_adder_3_carry_out, bcd_adder_4_carry_out, bcd_adder_5_carry_out,
       button_2_out, button_3_out, button_out, C_out, clock_1_out, comparator_1_gt, comparator_2_eq,
       comparator_2_gt, comparator_3_eq, comparator_3_gt, comparator_4_eq, comparator_4_gt, comparator_5_eq,
       minus_A_B_out, minus_A_out, minus_B_out, or_1_out, or_2_out, or_3_out, or_4_out, or_5_out, or_6_out,
       priority_encoder_1_gs, register_1_q, register_3_q, register_5_q, register_6_q, register_10_q,
       register_11_q, register_13_q, register_17_q, subtractor_1_bout, subtractor_2_bout, subtractor_3_bout,
       subtractor_4_bout, subtractor_5_bout;
  wire [3:0] bcd_adder_1_sum, bcd_adder_2_sum, bcd_adder_3_sum, bcd_adder_4_sum, bcd_adder_5_sum,
       multiplexer_1_out, multiplexer_1_out_2, multiplexer_1_out_3, multiplexer_1_out_4, multiplexer_1_out_5,
       multiplexer_2_out, multiplexer_2_out_2, multiplexer_2_out_3, multiplexer_2_out_4, multiplexer_2_out_5,
       multiplexer_3_out, multiplexer_4_out, multiplexer_5_out, multiplexer_6_out, multiplexer_6_out_2,
       multiplexer_6_out_3, multiplexer_6_out_4, multiplexer_6_out_5, multiplexer_7_out, negator_1_out,
       negator_2_out, negator_3_out, negator_4_out, priority_encoder_1_out, register_15_q, register_16_q,
       register_18_q, subtractor_1_out, subtractor_2_out, subtractor_3_out, subtractor_4_out,
       subtractor_5_out, subtractor_6_out, subtractor_7_out, subtractor_8_out, subtractor_9_out;
  wire [19:0] multiplexer_8_out, negator_5_out, register_9_q;
  wire [19:12] register_14_q;

  Button _2 (.out(_2_out));
  Button _1 (.out(_1_out));
  Button _4 (.out(_4_out));
  Button _5 (.out(_5_out));
  Button _7 (.out(_7_out));
  Button _8 (.out(_8_out));
  Button _0 (.out(_0_out));
  Clock clock_1 (.out(clock_1_out));
  Button button (.out(button_out));
  Button button_2 (.out(button_2_out));
  Button _3 (.out(_3_out));
  Button _6 (.out(_6_out));
  Button _9 (.out(_9_out));
  Button C (.out(C_out));
  Button button_3 (.out(button_3_out));
  or or_1 (or_1_out, button_out, button_2_out);
  Priority_Encoder #(.select(4)) priority_encoder_1 (
    .in0(_0_out), .in1(_1_out), .in2(_2_out), .in3(_3_out), .in4(_4_out), .in5(_5_out), .in6(_6_out),
    .in7(_7_out), .in8(_8_out), .in9(_9_out), .out(priority_encoder_1_out), .gs(priority_encoder_1_gs));  // open: in10, in11, in12, in13, in14, in15, en_out, en_in
  and and_1 (and_1_out, or_1_out, 1'b1);
  Register #(.width(1)) register_1 (.D(and_1_out), .en(or_1_out), .Q(register_1_q), .clk(clock_1_out), .clr(C_out));
  and and_2 (and_2_out, priority_encoder_1_gs, register_1_q);
  Register #(.width(4)) register_2 (
    .D(register_9_q[15:12]), .en(and_2_out), .Q(register_9_q[19:16]), .clk(clock_1_out), .clr(C_out));
  Register #(.width(1)) register_3 (.D(button_out), .en(or_1_out), .Q(register_3_q), .clk(clock_1_out), .clr(C_out));
  Register #(.width(4)) register_4 (
    .D(register_9_q[11:8]), .en(and_2_out), .Q(register_9_q[15:12]), .clk(clock_1_out), .clr(C_out));
  Register #(.width(1)) register_5 (.D(and_2_out), .en(and_2_out), .Q(register_5_q), .clk(clock_1_out), .clr(C_out));
  Register #(.width(1)) register_6 (
    .D(button_3_out), .en(register_5_q), .Q(register_6_q), .clk(clock_1_out), .clr(C_out));
  and and_3 (and_3_out, register_3_q, minus_A_B_out);
  and and_4 (and_4_out, ~register_3_q, B___A_out);  // AND_Gate
  Register #(.width(4)) register_7 (.en(and_2_out), .Q(register_9_q[11:8]), .clk(clock_1_out), .clr(C_out));  // open: D
  Register #(.width(4)) register_8 (
    .D(register_9_q[3:0]), .en(and_2_out), .Q(register_9_q[7:4]), .clk(clock_1_out), .clr(C_out));
  and and_5 (and_5_out, ~register_3_q, A___B_out);  // AND_Gate
  and and_6 (and_6_out, priority_encoder_1_gs, ~register_1_q);  // AND_Gate
  Register #(.width(4)) register_9 (
    .D(priority_encoder_1_out), .en(and_2_out), .Q(register_9_q[3:0]), .clk(clock_1_out), .clr(C_out));
  Register #(.width(1)) register_10 (
    .D(button_3_out), .en(register_13_q), .Q(register_10_q), .clk(clock_1_out), .clr(C_out));
  Register #(.width(1)) register_11 (
    .D(minus_B_out), .en(register_6_q), .Q(register_11_q), .clk(clock_1_out), .clr(C_out));
  and minus_A_B (minus_A_B_out, register_11_q, register_17_q);
  and and_7 (and_7_out, register_3_q, and_14_out);
  Register #(.width(4)) register_12 (
    .D(register_14_q[15:12]), .en(and_6_out), .Q(register_14_q[19:16]), .clk(clock_1_out), .clr(C_out));
  Register #(.width(1)) register_13 (.D(and_6_out), .en(and_6_out), .Q(register_13_q), .clk(clock_1_out), .clr(C_out));
  buf and_8 (and_8_out, register_6_q);  // AND_Gate
  and minus_A (minus_A_out, and_12_out, register_13_q);
  and minus_B (minus_B_out, register_5_q, and_8_out);
  and B___A (B___A_out, ~register_11_q, register_17_q);  // AND_Gate
  and and_9 (and_9_out, and_3_out, minus_A_B_out);
  and and_10 (and_10_out, B___A_out, ~and_4_out);  // AND_Gate
  and and_11 (and_11_out, minus_A_B_out, ~and_3_out);  // AND_Gate
  Register #(.width(4)) register_14 (
    .D(register_15_q), .en(and_6_out), .Q(register_14_q[15:12]), .clk(clock_1_out), .clr(C_out));
  and and_12 (and_12_out, register_10_q, ~register_5_q);  // AND_Gate
  and A___B (A___B_out, register_11_q, ~register_17_q);  // AND_Gate
  or or_2 (or_2_out, and_5_out, and_4_out, and_7_out, and_3_out);
  and and_13 (and_13_out, B___A_out, and_4_out);
  Register #(.width(4)) register_15 (
    .D(register_16_q), .en(and_6_out), .Q(register_15_q), .clk(clock_1_out), .clr(C_out));
  Register #(.width(4)) register_16 (
    .D(register_18_q), .en(and_6_out), .Q(register_16_q), .clk(clock_1_out), .clr(C_out));
  Register #(.width(1)) register_17 (
    .D(minus_A_out), .en(and_12_out), .Q(register_17_q), .clk(clock_1_out), .clr(C_out));
  and and_14 (and_14_out, ~register_11_q, ~register_17_q);  // AND_Gate
  or or_3 (or_3_out, and_10_out, and_11_out);
  Register #(.width(4)) register_18 (
    .D(priority_encoder_1_out), .en(and_6_out), .Q(register_18_q), .clk(clock_1_out), .clr(C_out));
  BCD_Adder bcd_adder_1 (
    .B(multiplexer_1_out_5), .A(multiplexer_2_out_5), .Sum(bcd_adder_1_sum), .Carry_in(bcd_adder_2_carry_out));  // open: Carry_Out
  and and_15 (and_15_out, A___B_out, ~or_5_out);  // AND_Gate
  and and_16 (and_16_out, or_5_out, or_4_out);
  or or_4 (or_4_out, and_13_out, and_9_out);
  Comparator #(.width(4)) comparator_1 (
    .a(register_18_q), .b(register_9_q[3:0]), .gt(comparator_1_gt));  // open: eq, lt
  Comparator #(.width(4)) comparator_2 (
    .a(register_16_q), .b(register_9_q[7:4]), .gt(comparator_2_gt), .eq(comparator_2_eq));  // open: lt
  Comparator #(.width(4)) comparator_3 (
    .a(register_15_q), .b(register_9_q[11:8]), .gt(comparator_3_gt), .eq(comparator_3_eq));  // open: lt
  Comparator #(.width(4)) comparator_4 (
    .a(register_14_q[15:12]), .b(register_9_q[15:12]), .gt(comparator_4_gt), .eq(comparator_4_eq));  // open: lt
  Comparator #(.width(4)) comparator_5 (
    .a(register_14_q[19:16]), .b(register_9_q[19:16]), .eq(comparator_5_eq));  // open: gt, lt
  BCD_Adder bcd_adder_2 (
    .Carry_Out(bcd_adder_2_carry_out), .B(multiplexer_2_out_4), .A(multiplexer_1_out_4),
    .Sum(bcd_adder_2_sum), .Carry_in(bcd_adder_3_carry_out));
  and and_17 (and_17_out, comparator_5_eq, comparator_4_eq, comparator_3_gt);
  and and_18 (and_18_out, comparator_5_eq, comparator_4_gt);
  or or_5 (or_5_out, and_18_out, and_17_out, and_20_out, and_19_out);
  BCD_Adder bcd_adder_3 (
    .Carry_Out(bcd_adder_3_carry_out), .B(multiplexer_2_out_3), .A(multiplexer_1_out_3),
    .Sum(bcd_adder_3_sum), .Carry_in(bcd_adder_4_carry_out));
  BCD_Adder bcd_adder_4 (
    .Carry_Out(bcd_adder_4_carry_out), .B(multiplexer_2_out_2), .A(multiplexer_1_out_2),
    .Sum(bcd_adder_4_sum), .Carry_in(bcd_adder_5_carry_out));
  and and_19 (and_19_out, comparator_5_eq, comparator_4_eq, comparator_3_eq, comparator_2_eq, comparator_1_gt);
  and and_20 (and_20_out, comparator_5_eq, comparator_4_eq, comparator_3_eq, comparator_2_gt);
  BCD_Adder bcd_adder_5 (
    .Carry_Out(bcd_adder_5_carry_out), .B(multiplexer_2_out), .A(multiplexer_1_out), .Sum(bcd_adder_5_sum),
    .Carry_in(1'b0));
  Multiplexer #(.width(20)) multiplexer_1 (
    .in0(register_9_q), .in1({register_14_q, register_15_q, register_16_q, register_18_q}),
    .out({multiplexer_1_out_5, multiplexer_1_out_4, multiplexer_1_out_3, multiplexer_1_out_2, multiplexer_1_out}),
    .sel(or_5_out));  // open: en
  or or_6 (or_6_out, and_15_out, and_16_out, or_3_out);
  Multiplexer #(.width(20)) multiplexer_2 (
    .in0({register_14_q, register_15_q, register_16_q, register_18_q}), .in1(register_9_q),
    .out({multiplexer_2_out_5, multiplexer_2_out_4, multiplexer_2_out_3, multiplexer_2_out_2, multiplexer_2_out}),
    .sel(or_5_out));  // open: en
  Subtractor #(.width(4)) subtractor_1 (
    .a(multiplexer_1_out), .b(multiplexer_2_out), .out(subtractor_1_out), .bin(1'b0), .bout(subtractor_1_bout));
  Subtractor #(.width(4)) subtractor_2 (
    .a(multiplexer_1_out_2), .b(multiplexer_2_out_2), .out(subtractor_2_out), .bin(subtractor_1_bout),
    .bout(subtractor_2_bout));
  Subtractor #(.width(4)) subtractor_3 (
    .a(multiplexer_1_out_3), .b(multiplexer_2_out_3), .out(subtractor_3_out), .bin(subtractor_2_bout),
    .bout(subtractor_3_bout));
  Subtractor #(.width(4)) subtractor_4 (
    .a(multiplexer_1_out_4), .b(multiplexer_2_out_4), .out(subtractor_4_out), .bin(subtractor_3_bout),
    .bout(subtractor_4_bout));
  Subtractor #(.width(4)) subtractor_5 (
    .a(multiplexer_1_out_5), .b(multiplexer_2_out_5), .out(subtractor_5_out), .bin(subtractor_4_bout),
    .bout(subtractor_5_bout));
  _7_Segment_Display u_7_segment_display_1 (.g(or_6_out));  // open: f, a, b, e, d, c, dp
  Hex_Digit_Display hex_digit_display_1 (.value(multiplexer_6_out_5));  // open: dp
  and and_21 (and_21_out, subtractor_1_bout, ~subtractor_5_bout);  // AND_Gate
  and and_22 (and_22_out, subtractor_3_bout, ~subtractor_5_bout);  // AND_Gate
  and and_23 (and_23_out, subtractor_4_bout, ~subtractor_5_bout);  // AND_Gate
  Hex_Digit_Display hex_digit_display_2 (.value(multiplexer_6_out_4));  // open: dp
  Multiplexer #(.width(4)) multiplexer_3 (
    .in0(subtractor_1_out), .in1(subtractor_8_out), .out(multiplexer_3_out), .sel(and_21_out));  // open: en
  and and_24 (and_24_out, subtractor_2_bout, ~subtractor_5_bout);  // AND_Gate
  Multiplexer #(.width(4)) multiplexer_4 (
    .in0(subtractor_3_out), .in1(subtractor_6_out), .out(multiplexer_4_out), .sel(and_22_out));  // open: en
  Multiplexer #(.width(4)) multiplexer_5 (
    .in0(subtractor_4_out), .in1(subtractor_7_out), .out(multiplexer_5_out), .sel(and_23_out));  // open: en
  Multiplexer #(.width(20)) multiplexer_6 (
    .in0({bcd_adder_1_sum, bcd_adder_2_sum, bcd_adder_3_sum, bcd_adder_4_sum, bcd_adder_5_sum}),
    .in1(multiplexer_8_out),
    .out({multiplexer_6_out_5, multiplexer_6_out_4, multiplexer_6_out_3, multiplexer_6_out_2, multiplexer_6_out}),
    .sel(or_2_out));  // open: en
  Hex_Digit_Display hex_digit_display_3 (.value(multiplexer_6_out_3));  // open: dp
  Hex_Digit_Display hex_digit_display_4 (.value(multiplexer_6_out_2));  // open: dp
  Negator #(.width(4)) negator_1 (.in(subtractor_1_out), .out(negator_1_out));
  Multiplexer #(.width(4)) multiplexer_7 (
    .in0(subtractor_2_out), .in1(subtractor_9_out), .out(multiplexer_7_out), .sel(and_24_out));  // open: en
  Negator #(.width(4)) negator_2 (.in(subtractor_3_out), .out(negator_2_out));
  Negator #(.width(4)) negator_3 (.in(subtractor_4_out), .out(negator_3_out));
  Hex_Digit_Display hex_digit_display_5 (.value(multiplexer_6_out));  // open: dp
  Negator #(.width(4)) negator_4 (.in(subtractor_2_out), .out(negator_4_out));
  Subtractor #(.width(4)) subtractor_6 (.a(in_3), .b(negator_2_out), .out(subtractor_6_out), .bin(1'b0));  // open: bout
  Subtractor #(.width(4)) subtractor_7 (.a(in_4), .b(negator_3_out), .out(subtractor_7_out), .bin(1'b0));  // open: bout
  Multiplexer #(.width(20)) multiplexer_8 (
    .in0({subtractor_5_out, multiplexer_5_out, multiplexer_4_out, multiplexer_7_out, multiplexer_3_out}),
    .in1(negator_5_out), .out(multiplexer_8_out), .sel(subtractor_5_bout));  // open: en
  Subtractor #(.width(4)) subtractor_8 (.a(in_1), .b(negator_1_out), .out(subtractor_8_out), .bin(1'b0));  // open: bout
  Subtractor #(.width(4)) subtractor_9 (.a(in_2), .b(negator_4_out), .out(subtractor_9_out), .bin(1'b0));  // open: bout
  Negator #(.width(20)) negator_5 (
    .in({subtractor_5_out, multiplexer_5_out, multiplexer_4_out, multiplexer_7_out, multiplexer_3_out}),
    .out(negator_5_out));

  // Notes on the sheet:
  //   You should press the negate button after entering a number that you want to negate
  //   Please set to 1010 before you start your calculations
  //   Please set to 1010 before you start your calculations
  //   Please set to 1010 before you start your calculations
  //   Please set to 1010 before you start your calculations
endmodule

module Half_Adder (
  input  in_1,
  input  in_2,
  output out_3,
  output out_4
);

  xor xor_1 (out_3, in_1, in_2);
  and and_1 (out_4, in_2, in_1);
endmodule

module Full_Adder (
  input  B,
  input  A,
  input  Carry_in,
  output Carry_Out,
  output S
);

  wire half_adder_1_out_3, half_adder_1_out_4, half_adder_2_out_4;

  Half_Adder half_adder_1 (.in_1(A), .in_2(B), .out_3(half_adder_1_out_3), .out_4(half_adder_1_out_4));
  Half_Adder half_adder_2 (.in_1(Carry_in), .in_2(half_adder_1_out_3), .out_3(S), .out_4(half_adder_2_out_4));
  or or_1 (Carry_Out, half_adder_2_out_4, half_adder_1_out_4);
endmodule

module _4_bit_Binary_Adder (
  input  [3:0] B,
  input  [3:0] A,
  input  Carry_in,
  output Carry_out,
  output S3,
  output S2,
  output S1,
  output S0
);

  wire full_adder_2_carry_out, full_adder_3_carry_out, full_adder_4_carry_out;

  Full_Adder full_adder_1 (.Carry_Out(Carry_out), .B(B[3]), .A(A[3]), .S(S3), .Carry_in(full_adder_2_carry_out));
  Full_Adder full_adder_2 (
    .Carry_Out(full_adder_2_carry_out), .B(B[2]), .A(A[2]), .S(S2), .Carry_in(full_adder_3_carry_out));
  Full_Adder full_adder_3 (
    .Carry_Out(full_adder_3_carry_out), .B(B[1]), .A(A[1]), .S(S1), .Carry_in(full_adder_4_carry_out));
  Full_Adder full_adder_4 (.Carry_Out(full_adder_4_carry_out), .B(B[0]), .A(A[0]), .S(S0), .Carry_in(Carry_in));
endmodule

module BCD_Adder (
  input  [3:0] A,
  input  [3:0] B,
  input  Carry_in,
  output Carry_Out,
  output [3:0] Sum
);

  wire and_1_out, n4_bit_binary_adder_1_carry_out, or_2_out;
  wire [3:0] n4_bit_binary_adder_1_s0;

  or or_1 (Carry_Out, n4_bit_binary_adder_1_carry_out, and_1_out);
  and and_1 (and_1_out, n4_bit_binary_adder_1_s0[3], or_2_out);
  or or_2 (or_2_out, n4_bit_binary_adder_1_s0[2], n4_bit_binary_adder_1_s0[1]);
  _4_bit_Binary_Adder u_4_bit_binary_adder_1 (
    .Carry_out(n4_bit_binary_adder_1_carry_out), .B(B), .A(A), .S3(n4_bit_binary_adder_1_s0[3]),
    .S2(n4_bit_binary_adder_1_s0[2]), .S1(n4_bit_binary_adder_1_s0[1]), .S0(n4_bit_binary_adder_1_s0[0]),
    .Carry_in(Carry_in));
  _4_bit_Binary_Adder u_4_bit_binary_adder_2 (
    .B(n4_bit_binary_adder_1_s0), .A({1'b0, {2{Carry_Out}}, 1'b0}), .S3(Sum[3]), .S2(Sum[2]), .S1(Sum[1]),
    .S0(Sum[0]), .Carry_in(1'b0));  // open: Carry_out
endmodule

module BCD_Subtractor (
  input  [3:0] B,
  input  [3:0] A,
  input  in_3,
  output [3:0] Sub
);

  wire bcd_adder_1_carry_out;
  wire [3:0] bcd_adder_1_sum, n4_bit_binary_adder_1_s0, xor_4_out, xor_8_out;
  wire [3:3] not_1_out;

  xor xor_1 (xor_4_out[3], B[3], 1'b1);
  xor xor_2 (xor_4_out[1], B[1], 1'b1);
  xor xor_3 (xor_4_out[2], B[2], 1'b1);
  not not_1 (not_1_out[3], bcd_adder_1_carry_out);
  xor xor_4 (xor_4_out[0], B[0], 1'b1);
  xor xor_5 (xor_8_out[2], not_1_out[3], bcd_adder_1_sum[2]);
  xor xor_6 (xor_8_out[3], not_1_out[3], bcd_adder_1_sum[3]);
  _4_bit_Binary_Adder u_4_bit_binary_adder_1 (
    .B(xor_4_out), .A(4'b1010), .S3(n4_bit_binary_adder_1_s0[3]), .S2(n4_bit_binary_adder_1_s0[2]),
    .S1(n4_bit_binary_adder_1_s0[1]), .S0(n4_bit_binary_adder_1_s0[0]), .Carry_in(1'b0));  // open: Carry_out
  BCD_Adder bcd_adder_1 (
    .Carry_Out(bcd_adder_1_carry_out), .B(n4_bit_binary_adder_1_s0), .A(A), .Sum(bcd_adder_1_sum),
    .Carry_in(in_3));
  xor xor_7 (xor_8_out[1], not_1_out[3], bcd_adder_1_sum[1]);
  xor xor_8 (xor_8_out[0], not_1_out[3], bcd_adder_1_sum[0]);
  _4_bit_Binary_Adder u_4_bit_binary_adder_2 (
    .B(xor_8_out), .A({not_1_out[3], 1'b0, not_1_out[3], 1'b0}), .S3(Sub[3]), .S2(Sub[2]), .S1(Sub[1]),
    .S0(Sub[0]), .Carry_in(bcd_adder_1_carry_out));  // open: Carry_out
endmodule

module Binary_Subtractor (
  input  [3:0] B,
  input  [3:0] A,
  input  in_3,
  output Borrow_out,
  output [3:0] Sub
);

  wire [3:0] not_1_out;

  assign not_1_out = ~B;  // NOT_Gate not_1, 4 bits wide
  _4_bit_Binary_Adder u_4_bit_binary_adder_1 (
    .Carry_out(Borrow_out), .B(not_1_out), .A(A), .S3(Sub[3]), .S2(Sub[2]), .S1(Sub[1]), .S0(Sub[0]),
    .Carry_in(in_3));
endmodule

module Half_Subtractor (
  input  A,
  input  B,
  output Diff,
  output Borrow
);

  wire not_1_out;

  not not_1 (not_1_out, A);
  xor xor_1 (Diff, A, B);
  and and_1 (Borrow, not_1_out, B);
endmodule

module Full_Subtractor (
  input  A,
  input  B,
  input  Borrow_in,
  output Borrow_out,
  output Diff
);

  wire half_subtractor_1_borrow, half_subtractor_1_diff, half_subtractor_2_borrow;

  Half_Subtractor half_subtractor_1 (.A(A), .B(B), .Diff(half_subtractor_1_diff), .Borrow(half_subtractor_1_borrow));
  Half_Subtractor half_subtractor_2 (
    .A(half_subtractor_1_diff), .B(Borrow_in), .Diff(Diff), .Borrow(half_subtractor_2_borrow));
  or or_1 (Borrow_out, half_subtractor_2_borrow, half_subtractor_1_borrow);
endmodule

module _4_bit_Subtractor (
  input  [3:0] B,
  input  [3:0] A,
  input  in_3,
  output out_4,
  output [3:0] Sum
);

  wire full_subtractor_1_borrow_out, full_subtractor_2_borrow_out, full_subtractor_3_borrow_out;

  Full_Subtractor full_subtractor_1 (
    .A(A[3]), .B(B[3]), .Borrow_out(full_subtractor_1_borrow_out), .Borrow_in(in_3), .Diff(Sum[3]));
  Full_Subtractor full_subtractor_2 (
    .A(A[2]), .B(B[2]), .Borrow_out(full_subtractor_2_borrow_out), .Borrow_in(full_subtractor_1_borrow_out),
    .Diff(Sum[2]));
  Full_Subtractor full_subtractor_3 (
    .A(A[1]), .B(B[1]), .Borrow_out(full_subtractor_3_borrow_out), .Borrow_in(full_subtractor_2_borrow_out),
    .Diff(Sum[1]));
  Full_Subtractor full_subtractor_4 (
    .A(A[0]), .B(B[0]), .Borrow_out(out_4), .Borrow_in(full_subtractor_3_borrow_out), .Diff(Sum[0]));
endmodule
