// Logisim project KeyPad.circ as structural Verilog: 1 circuit, main circuit main
// ggh
module main (
);

  wire and_1_out, and_2_out, and_3_out, and_4_out, and_5_out, and_6_out, and_7_out, clock_1_out, K1_out,
       K2_out, K3_out, Ko_out, or_1_out, or_2_out, register_1_q, register_2_q, register_3_q, register_4_q,
       register_5_q, register_6_q, register_7_q, register_8_q, register_9_q, register_10_q, RESET_out;

  Clock clock_1 (.out(clock_1_out));
  Register #(.width(1)) register_1 (.D(1'b1), .en(K2_out), .Q(register_1_q), .clk(clock_1_out), .clr(RESET_out));
  Register #(.width(1)) register_2 (.D(1'b1), .en(K3_out), .Q(register_2_q), .clk(clock_1_out), .clr(RESET_out));
  Register #(.width(1)) register_3 (.D(1'b1), .en(K1_out), .Q(register_3_q), .clk(clock_1_out), .clr(RESET_out));
  Register #(.width(1)) register_4 (.D(1'b1), .en(Ko_out), .Q(register_4_q), .clk(clock_1_out), .clr(RESET_out));
  and and_1 (and_1_out, register_4_q, register_3_q, ~register_2_q, ~register_1_q);  // AND_Gate
  and and_2 (and_2_out, register_5_q, register_1_q);
  and and_3 (and_3_out, ~register_5_q, register_3_q, register_1_q);  // AND_Gate
  and and_4 (and_4_out, register_6_q, register_2_q);
  and and_5 (and_5_out, register_7_q, register_2_q);
  and and_6 (and_6_out, ~register_4_q, register_1_q, register_2_q, ~register_3_q);  // AND_Gate
  and and_7 (and_7_out, ~and_1_out, ~and_2_out, ~and_4_out, ~and_3_out, ~and_5_out, ~and_6_out);  // AND_Gate
  or or_1 (or_1_out, and_7_out, RESET_out);
  Register #(.width(1)) register_5 (.D(1'b1), .en(and_1_out), .Q(register_5_q), .clk(clock_1_out), .clr(or_1_out));
  Register #(.width(1)) register_6 (.D(1'b1), .en(and_2_out), .Q(register_6_q), .clk(clock_1_out), .clr(or_1_out));
  Register #(.width(1)) register_7 (.D(1'b1), .en(and_3_out), .Q(register_7_q), .clk(clock_1_out), .clr(or_1_out));
  Register #(.width(1)) register_8 (.D(1'b1), .en(and_4_out), .Q(register_8_q), .clk(clock_1_out), .clr(or_1_out));
  Register #(.width(1)) register_9 (.D(1'b1), .en(and_5_out), .Q(register_9_q), .clk(clock_1_out), .clr(or_1_out));
  Register #(.width(1)) register_10 (.D(1'b1), .en(and_6_out), .Q(register_10_q), .clk(clock_1_out), .clr(or_1_out));
  Button Ko (.out(Ko_out));
  Button K1 (.out(K1_out));
  Button K2 (.out(K2_out));
  or or_2 (or_2_out, register_5_q, register_6_q, register_7_q, register_8_q, register_9_q, register_10_q);
  Button K3 (.out(K3_out));
  Button RESET (.out(RESET_out));
  LED led_1 (.in(or_2_out));
endmodule
