// Logisim project Traffic light.circ as structural Verilog: 4 circuits, main circuit Traffic Light
module D_Flip_Flop (
  input  in_1,
  input  in_2,
  output out_3,
  output out_4
);

  wire and_1_out, and_2_out, and_3_out, and_4_out, nor_1_out, nor_2_out, not_1_out;

  not not_1 (not_1_out, in_1);
  and and_1 (and_1_out, not_1_out, ~in_2);  // AND_Gate
  and and_2 (and_2_out, not_1_out, in_2);
  nor nor_1 (nor_1_out, and_1_out, nor_2_out);
  nor nor_2 (nor_2_out, nor_1_out, and_2_out);
  and and_3 (and_3_out, in_1, ~nor_1_out);  // AND_Gate
  and and_4 (and_4_out, in_1, nor_1_out);
  nor nor_3 (out_3, and_3_out, out_4);
  nor nor_4 (out_4, out_3, and_4_out);
endmodule

module Resettable (
  input  in_1,
  input  in_2,
  input  in_3,
  output out_4,
  output out_5
);

  wire and_1_out;

  and and_1 (and_1_out, in_2, ~in_3);  // AND_Gate
  D_Flip_Flop d_flip_flop_1 (.in_1(in_1), .in_2(and_1_out), .out_3(out_4), .out_4(out_5));
endmodule

module _3_bit_Counter (
  input  in_1
);

  wire and_1_out, and_2_out, clock_1_out, resettable_1_out_4, resettable_2_out_4, resettable_3_out_4,
       xor_1_out, xor_2_out, xor_3_out;

  xor xor_1 (xor_1_out, 1'b1, resettable_1_out_4);
  Clock clock_1 (.out(clock_1_out));
  Resettable resettable_1 (
    .in_1(clock_1_out), .in_2(xor_1_out), .in_3(in_1), .out_4(resettable_1_out_4));  // open: out_5
  xor xor_2 (xor_2_out, resettable_1_out_4, resettable_2_out_4);
  Resettable resettable_2 (
    .in_1(clock_1_out), .in_2(xor_2_out), .in_3(in_1), .out_4(resettable_2_out_4));  // open: out_5
  and and_1 (and_1_out, resettable_2_out_4, resettable_1_out_4);
  xor xor_3 (xor_3_out, and_1_out, resettable_3_out_4);
  Resettable resettable_3 (
    .in_1(clock_1_out), .in_2(xor_3_out), .in_3(in_1), .out_4(resettable_3_out_4));  // open: out_5
  and and_2 (and_2_out, resettable_3_out_4, and_1_out);
  LED led_1 (.in(resettable_2_out_4));
  LED led_2 (.in(resettable_3_out_4));
  LED led_3 (.in(resettable_1_out_4));
endmodule

module Traffic_Light (
  input  in_1
);

  wire and_1_out, and_2_out, and_3_out, and_4_out, and_5_out, and_6_out, and_7_out, and_8_out, and_9_out,
       and_10_out, clock_1_out, Green___31_out, or_1_out, or_2_out, or_3_out, Red___7_out,
       resettable_1_out_4, resettable_2_out_4, resettable_3_out_4, resettable_4_out_4, resettable_5_out_4,
       resettable_6_out_4, resettable_7_out_4, xor_1_out, xor_2_out, xor_3_out, xor_4_out, xor_5_out,
       xor_6_out, xor_7_out, Yellow___2_out;

  xor xor_1 (xor_1_out, 1'b1, resettable_1_out_4);
  Clock clock_1 (.out(clock_1_out));
  Resettable resettable_1 (
    .in_1(clock_1_out), .in_2(xor_1_out), .in_3(or_1_out), .out_4(resettable_1_out_4));  // open: out_5
  or or_1 (or_1_out, in_1, or_2_out);
  xor xor_2 (xor_2_out, resettable_1_out_4, resettable_2_out_4);
  and and_1 (and_1_out, resettable_2_out_4, resettable_1_out_4);
  Resettable resettable_2 (
    .in_1(clock_1_out), .in_2(xor_2_out), .in_3(or_1_out), .out_4(resettable_2_out_4));  // open: out_5
  xor xor_3 (xor_3_out, and_1_out, resettable_3_out_4);
  Resettable resettable_3 (
    .in_1(clock_1_out), .in_2(xor_3_out), .in_3(or_1_out), .out_4(resettable_3_out_4));  // open: out_5
  and and_2 (and_2_out, resettable_3_out_4, and_1_out);
  xor xor_4 (xor_4_out, and_2_out, resettable_4_out_4);
  and and_3 (and_3_out, resettable_4_out_4, and_2_out);
  Resettable resettable_4 (
    .in_1(clock_1_out), .in_2(xor_4_out), .in_3(or_1_out), .out_4(resettable_4_out_4));  // open: out_5
  xor xor_5 (xor_5_out, and_3_out, resettable_5_out_4);
  Resettable resettable_5 (
    .in_1(clock_1_out), .in_2(xor_5_out), .in_3(or_1_out), .out_4(resettable_5_out_4));  // open: out_5
  and Red___7 (Red___7_out, ~resettable_5_out_4, ~resettable_4_out_4, resettable_3_out_4, resettable_2_out_4, resettable_1_out_4);  // AND_Gate
  and and_4 (and_4_out, Red___7_out, and_7_out);
  and Yellow___2 (Yellow___2_out, ~resettable_5_out_4, ~resettable_4_out_4, ~resettable_3_out_4, resettable_2_out_4, ~resettable_1_out_4);  // AND_Gate
  and and_5 (and_5_out, Yellow___2_out, or_3_out);
  or or_2 (or_2_out, and_4_out, and_5_out, and_6_out);
  xor xor_6 (xor_6_out, or_2_out, resettable_6_out_4);
  and Green___31 (Green___31_out, resettable_5_out_4, resettable_4_out_4, resettable_3_out_4, resettable_2_out_4, resettable_1_out_4);
  and and_6 (and_6_out, Green___31_out, and_10_out);
  Resettable resettable_6 (
    .in_1(clock_1_out), .in_2(xor_6_out), .in_3(in_1), .out_4(resettable_6_out_4));  // open: out_5
  xor xor_7 (xor_7_out, resettable_6_out_4, resettable_7_out_4);
  Resettable resettable_7 (
    .in_1(clock_1_out), .in_2(xor_7_out), .in_3(in_1), .out_4(resettable_7_out_4));  // open: out_5
  and and_7 (and_7_out, ~resettable_6_out_4, ~resettable_7_out_4);  // AND_Gate
  and and_8 (and_8_out, resettable_6_out_4, resettable_7_out_4);
  and and_9 (and_9_out, resettable_6_out_4, ~resettable_7_out_4);  // AND_Gate
  and and_10 (and_10_out, ~resettable_6_out_4, resettable_7_out_4);  // AND_Gate
  or or_3 (or_3_out, and_8_out, and_9_out);
  LED led_1 (.in(and_7_out));
  LED led_2 (.in(or_3_out));
  LED led_3 (.in(and_10_out));
endmodule
